// Logisim project 1b ALU.circ as structural Verilog: 1 circuit, main circuit 1b ALU
// cin
module _1b_ALU (
  input  sub,
  input  cin,
  input  A,
  input  [2:0] in_4,
  input  B,
  input  cout,
  output Result
);

  wire adder_1_out, and_1_out, not_1_out, or_1_out, xor_1_out, xor_2_out;

  xor xor_1 (xor_1_out, B, sub);
  not not_1 (not_1_out, A);
  and and_1 (and_1_out, A, B);
  or or_1 (or_1_out, A, B);
  xor xor_2 (xor_2_out, A, B);
  Adder #(.width(1)) adder_1 (.a(A), .b(xor_1_out), .out(adder_1_out), .cin(cin), .cout(cout));
  Multiplexer #(.select(3), .enable("false")) multiplexer_1 (
    .in0(not_1_out), .in1(and_1_out), .in2(or_1_out), .in3(xor_2_out), .in4(adder_1_out), .out(Result),
    .sel(in_4));  // open: in5, in6, in7
endmodule
